# Fritzing sketch Joystick Emulator v21 (saved by Fritzing 0.9.2b)
circuit board: 6.04397cm x 1.95495cm
breadboards: 1

parts:
  74LS05 = IC, DIP package, 14 pins [chip_label=74LS05]
  5 = Header 1 [package=luxeon-pad]  # not connected
  4 = Header 1 [package=luxeon-pad]
  3 = Header 1 [package=luxeon-pad]
  2 = Header 1 [package=luxeon-pad]
  1 = Header 1 [package=luxeon-pad]
  Arduino_Nano = Arduino Nano (Rev3.0)
  9 = Header 1 [package=luxeon-pad]  # not connected
  8 = Header 1 [package=luxeon-pad]
  7 = Header 1 [package=luxeon-pad]
  6 = Header 1 [package=luxeon-pad]
  J1 = male pin header, 2 pins [form="♂ (male)"]

nets:
  N1: 74LS05.pin1, Arduino_Nano.D2
  N2: 74LS05.pin2, 1.1
  N3: 74LS05.pin3, Arduino_Nano.D3
  N4: 74LS05.pin4, 2.1
  N5: 74LS05.pin5, Arduino_Nano.D4
  N6: 74LS05.pin6, 3.1
  GND: 74LS05.pin7, Arduino_Nano.GND, 8.1
  N7: 74LS05.pin8, 4.1
  N8: 74LS05.pin9, Arduino_Nano.D5
  N9: 74LS05.pin10, 6.1
  N10: 74LS05.pin11, Arduino_Nano.D6
  5V: 74LS05.pin14, Arduino_Nano.5V, J1.pin2
  N11: 7.1, J1.pin1

notes:
  1=Up
  2=Down
  3=Left
  4=Right
  5=PotY
  6=Fire
  7=5V
  8=GND
  9=PotX
  Other Side Up!
  Leif Bloomquist
  Joystick Emulator
  2015 0v2
