# Fritzing sketch Joystick Emulator v46 0v3 (saved by Fritzing 0.9.2b)
circuit board: 5.87847cm x 2.49531cm
breadboards: 1

parts:
  74LS05 = IC, DIP package, 14 pins [chip_label=74LS05]
  5 = Header 1 [package=luxeon-pad]
  4 = Header 1 [package=luxeon-pad]
  3 = Header 1 [package=luxeon-pad]
  2 = Header 1 [package=luxeon-pad]
  1 = Header 1 [package=luxeon-pad]
  9 = Header 1 [package=luxeon-pad]
  8 = Header 1 [package=luxeon-pad]
  7 = Header 1 [package=luxeon-pad]
  6 = Header 1 [package=luxeon-pad]
  J1 = male pin header, 2 pins [form="♂ (male)"]
  J2 = male pin header, 15 pins [form="♂ (male)"]
  J3 = male pin header, 15 pins [form="♂ (male)"]
  R2 = Resistor [tolerance=±5% resistance=4.7k package=THT]
  R1 = Resistor [tolerance=±5% resistance=4.7k package=THT]
  Arduino_Nano = Arduino Nano (Rev3.0)

nets:
  N1: 74LS05.pin1, J3.pin5, Arduino_Nano.D2
  N2: 74LS05.pin2, 1.1
  N3: 74LS05.pin3, J3.pin6, Arduino_Nano.D3
  N4: 74LS05.pin4, 2.1
  N5: 74LS05.pin5, J3.pin7, Arduino_Nano.D4
  N6: 74LS05.pin6, 3.1
  GND: 74LS05.pin7, 8.1, J2.pin2, J3.pin4, Arduino_Nano.GND
  N7: 74LS05.pin8, 4.1
  N8: 74LS05.pin9, J3.pin8, Arduino_Nano.D5
  N9: 74LS05.pin10, 6.1
  N10: 74LS05.pin11, J3.pin9, Arduino_Nano.D6
  5V: 74LS05.pin14, J1.pin2, J2.pin4, Arduino_Nano.5V
  POTY: 5.1, R1.Pin_1
  POTX: 9.1, J3.pin10, R2.Pin_1, Arduino_Nano.D7
  N11: 7.1, J1.pin1
  N12: J2.pin1, Arduino_Nano.VIN
  N13: J2.pin3, J3.pin3, Arduino_Nano.RESET
  N14: J2.pin5, Arduino_Nano.A7
  N15: J2.pin6, Arduino_Nano.A6
  N16: J2.pin7, Arduino_Nano.A5
  N17: J2.pin8, Arduino_Nano.A4
  N18: J2.pin9, Arduino_Nano.A3
  N19: J2.pin10, Arduino_Nano.A2
  N20: J2.pin11, Arduino_Nano.A1
  N21: J2.pin12, Arduino_Nano.A0
  N22: J2.pin13, Arduino_Nano.AREF
  N23: J2.pin14, Arduino_Nano.3V3
  N24: J2.pin15, Arduino_Nano.D13/SCK
  N25: J3.pin1, Arduino_Nano.D1/TX
  N26: J3.pin2, Arduino_Nano.D0/RX
  N27: J3.pin11, R2.Pin_0, Arduino_Nano.D8
  N28: J3.pin12, R1.Pin_0, Arduino_Nano.D9
  N29: J3.pin13, Arduino_Nano.D10
  N30: J3.pin14, Arduino_Nano.D11/MOSI
  N31: J3.pin15, Arduino_Nano.D12/MISO

notes:
  C64 Control Port Pins
  1=Up
  2=Down
  3=Left
  4=Right
  5=PotY
  6=Fire
  7=5V
  8=GND
  9=PotX
  Arduino Nano Pins
  D0=RX (USB Reserved)
  D1=TX (USB Reserved)
  D2=Joystick Up (Output)
  D3=Joystick Down (Output)
  D4=Joystick Left (Output)
  D5=Joystick Right (Output)
  D6=Joystick Fire (Output)
  D7=POTX Sense (Input)
  D8=POTX PWM (Output)
  D9=POTY PWM (Output)
  Joystick / Paddle / Mouse
  Leif Bloomquist
  2015 0v3
  Emulator for C64
